// Logisim project hc01.circ as structural Verilog: 7 circuits, main circuit NotGate
module NotGate (
  input  a,
  output nota
);

  nand nand_1 (nota, a, a);
endmodule

module AndGate (
  input  a,
  input  b,
  output aandb
);

  wire nand_1_out;

  nand nand_1 (nand_1_out, a, b);
  NotGate notgate_1 (.nota(aandb), .a(nand_1_out));
endmodule

module OrGate (
  input  a,
  input  b,
  output aorb
);

  wire notgate_1_nota, notgate_2_nota;

  NotGate notgate_1 (.nota(notgate_1_nota), .a(a));
  NotGate notgate_2 (.nota(notgate_2_nota), .a(b));
  nand nand_1 (aorb, notgate_1_nota, notgate_2_nota);
endmodule

module XorGate (
  input  a,
  input  b,
  output axorb
);

  wire andgate_1_aandb, andgate_2_aandb, notgate_1_nota, notgate_2_nota;

  NotGate notgate_1 (.nota(notgate_1_nota), .a(a));
  NotGate notgate_2 (.nota(notgate_2_nota), .a(b));
  AndGate andgate_1 (.aandb(andgate_1_aandb), .b(b), .a(notgate_1_nota));
  AndGate andgate_2 (.aandb(andgate_2_aandb), .b(notgate_2_nota), .a(a));
  OrGate orgate_1 (.aorb(axorb), .a(andgate_1_aandb), .b(andgate_2_aandb));
endmodule

module MuxGate (
  input  a,
  input  sel,
  input  b,
  output muxab
);

  wire andgate_1_aandb, andgate_2_aandb, notgate_1_nota;

  NotGate notgate_1 (.nota(notgate_1_nota), .a(sel));
  AndGate andgate_1 (.aandb(andgate_1_aandb), .b(notgate_1_nota), .a(a));
  AndGate andgate_2 (.aandb(andgate_2_aandb), .b(b), .a(sel));
  OrGate orgate_1 (.aorb(muxab), .a(andgate_1_aandb), .b(andgate_2_aandb));
endmodule

module DMuxGate (
  input  inbit,
  input  sel,
  output a,
  output b
);

  wire notgate_1_nota;

  NotGate notgate_1 (.nota(notgate_1_nota), .a(sel));
  AndGate andgate_1 (.aandb(a), .b(notgate_1_nota), .a(inbit));
  AndGate andgate_2 (.aandb(b), .b(inbit), .a(sel));
endmodule

module Not16 (
  input  [15:0] in16bit,
  output [15:0] out16bit
);

  NotGate notgate_1 (.nota(out16bit[0]), .a(in16bit[0]));
  NotGate notgate_2 (.nota(out16bit[1]), .a(in16bit[1]));
  NotGate notgate_3 (.nota(out16bit[2]), .a(in16bit[2]));
  NotGate notgate_4 (.nota(out16bit[3]), .a(in16bit[3]));
  NotGate notgate_5 (.nota(out16bit[4]), .a(in16bit[4]));
  NotGate notgate_6 (.nota(out16bit[5]), .a(in16bit[5]));
  NotGate notgate_7 (.nota(out16bit[6]), .a(in16bit[6]));
  NotGate notgate_8 (.nota(out16bit[7]), .a(in16bit[7]));
  NotGate notgate_9 (.nota(out16bit[8]), .a(in16bit[8]));
  NotGate notgate_10 (.nota(out16bit[9]), .a(in16bit[9]));
  NotGate notgate_11 (.nota(out16bit[10]), .a(in16bit[10]));
  NotGate notgate_12 (.nota(out16bit[11]), .a(in16bit[11]));
  NotGate notgate_13 (.nota(out16bit[12]), .a(in16bit[12]));
  NotGate notgate_14 (.nota(out16bit[13]), .a(in16bit[13]));
  NotGate notgate_15 (.nota(out16bit[14]), .a(in16bit[14]));
  NotGate notgate_16 (.nota(out16bit[15]), .a(in16bit[15]));
endmodule
